// Logisim project datapath.circ as structural Verilog: 1 circuit, main circuit main
module main (
  input  in_1
);

  wire alu_8_bit_1_zero, and_1_out, clock_1_out, not_1_out, not_2_out, undriven, undriven_2, undriven_4,
       undriven_5;
  wire [7:0] alu_8_bit_1_s, full_adder_8_bit_1_z, full_adder_8_bit_2_z, multiplexer_1_out, multiplexer_2_out,
       multiplexer_3_out, ram_2_data, reg8b_1_q, regfile_1_aval, regfile_1_bval, undriven_3;

  Multiplexer #(.width(8)) multiplexer_1 (
    .in0(full_adder_8_bit_2_z), .in1(full_adder_8_bit_1_z), .out(multiplexer_1_out), .sel(and_1_out));  // open: en
  Clock clock_1 (.out(clock_1_out));
  and and_1 (and_1_out, alu_8_bit_1_zero, undriven_2);
  Full_Adder_8_bit full_adder_8_bit_1 (.Ci(1'b0), .X(reg8b_1_q), .Y(undriven_3), .Z(full_adder_8_bit_1_z));
  Reg8b reg8b_1 (.EN(undriven), .CLK(clock_1_out), .D(multiplexer_1_out), .Q(reg8b_1_q), .Reset_n(in_1));
  Full_Adder_8_bit full_adder_8_bit_2 (.Ci(1'b0), .X(reg8b_1_q), .Y(8'h1), .Z(full_adder_8_bit_2_z));
  RAM #(.dataWidth(16), .bus("separate")) ram_1 (
    .addr(reg8b_1_q), .clk(clock_1_out), .clr(not_1_out));  // open: din, data, str, sel, ld
  not not_1 (not_1_out, in_1);
  RegFile regfile_1 (
    .Data(multiplexer_3_out), .Aval(regfile_1_aval), .Bval(regfile_1_bval), .CLK(clock_1_out), .Reset_n(in_1));  // open: Dmsel, Sel, Areg, Breg, _0, _1, _2, _3
  Multiplexer #(.width(8)) multiplexer_2 (
    .in0(regfile_1_bval), .in1(undriven_3), .out(multiplexer_2_out), .sel(undriven_5));  // open: en
  Multiplexer #(.width(8)) multiplexer_3 (
    .in0(ram_2_data), .in1(alu_8_bit_1_s), .out(multiplexer_3_out), .sel(undriven_4));  // open: en
  ALU_8_bit alu_8_bit_1 (
    .Zero(alu_8_bit_1_zero), .A(regfile_1_aval), .B(multiplexer_2_out), .S(alu_8_bit_1_s));  // open: Neg, Over, Co, Op
  RAM #(.bus("separate")) ram_2 (
    .addr(alu_8_bit_1_s), .din(regfile_1_bval), .data(ram_2_data), .clk(clock_1_out), .clr(not_2_out));  // open: str, sel, ld
  not not_2 (not_2_out, in_1);
endmodule
